// Logisim project 4bitadder.circ as structural Verilog: 1 circuit, main circuit main
module main (
  input  a0,
  input  b0,
  input  a1,
  input  b1,
  input  a2,
  input  b2,
  input  a3,
  input  b3
);

  wire and_1_out, and_2_out, and_3_out, and_4_out, and_5_out, and_6_out, and_7_out, or_1_out, or_2_out,
       or_3_out, xor_1_out, xor_2_out, xor_3_out, xor_4_out, xor_5_out, xor_6_out, xor_7_out;

  xor xor_1 (xor_1_out, a0, b0);
  and and_1 (and_1_out, a0, b0);
  and and_2 (and_2_out, a1, b1);
  xor xor_2 (xor_2_out, a1, b1);
  xor xor_3 (xor_3_out, a2, b2);
  and and_3 (and_3_out, a2, b2);
  LED led_1 (.in(xor_1_out));
  xor xor_4 (xor_4_out, and_1_out, xor_2_out);
  and and_4 (and_4_out, and_1_out, xor_2_out);
  or or_1 (or_1_out, and_4_out, and_2_out);
  LED led_2 (.in(xor_4_out));
  xor xor_5 (xor_5_out, or_1_out, xor_3_out);
  LED led_3 (.in(xor_5_out));
  and and_5 (and_5_out, xor_3_out, or_1_out);
  or or_2 (or_2_out, and_5_out, and_3_out);
  xor xor_6 (xor_6_out, a3, b3);
  and and_6 (and_6_out, a3, b3);
  xor xor_7 (xor_7_out, or_2_out, xor_6_out);
  and and_7 (and_7_out, or_2_out, xor_6_out);
  LED led_4 (.in(xor_7_out));
  or or_3 (or_3_out, and_7_out, and_6_out);
  LED led_5 (.in(or_3_out));

  // Notes on the sheet:
  //   s0
  //   s1
  //   s2
  //   s3
  //   s4
endmodule
