// Logisim project Fulladder.circ as structural Verilog: 1 circuit, main circuit main
module main (
  input  Input_1,
  input  Input_2,
  input  Carry_in
);

  wire and_1_out, and_2_out, or_1_out, xor_1_out, xor_2_out;

  and and_1 (and_1_out, Input_1, Input_2);
  xor xor_1 (xor_1_out, Input_1, Input_2);
  and and_2 (and_2_out, xor_1_out, Carry_in);
  xor xor_2 (xor_2_out, xor_1_out, Carry_in);
  or or_1 (or_1_out, and_1_out, and_2_out);
  LED led_1 (.in(or_1_out));
  LED led_2 (.in(xor_2_out));

  // Notes on the sheet:
  //   Carry output
  //   Sum output
endmodule
