// Logisim project S-R_Flip_Flop.circ as structural Verilog: 1 circuit, main circuit main
module main (
  input  S,
  input  R
);

  wire nor_1_out, nor_2_out;

  nor nor_1 (nor_1_out, S, nor_2_out);
  nor nor_2 (nor_2_out, nor_1_out, R);
  LED led_1 (.in(nor_1_out));
  LED led_2 (.in(nor_2_out));

  // Notes on the sheet:
  //   Q
  //   Q'
endmodule
