// Logisim project Encounter.circ as structural Verilog: 1 circuit, main circuit main
module main (
  input  in_1,
  input  in_2,
  input  Input_1
);

  wire and_1_out, and_2_out, not_1_out, or_1_out;

  not not_1 (not_1_out, Input_1);
  and and_1 (and_1_out, in_2, not_1_out);
  and and_2 (and_2_out, Input_1, in_1);
  or or_1 (or_1_out, and_1_out, and_2_out);
  LED led_1 (.in(or_1_out));

  // Notes on the sheet:
  //   Input2
  //   Input3
  //   encounter
  //   Output
endmodule
